// Logisim project Projec.circ as structural Verilog: 1 circuit, main circuit main
module main (
  input  [7:0] in_1
);

  wire and_1_out, clock_1_out, CLR, comparator_3_eq, comparator_4_eq, decoder_1_out0, decoder_1_out1,
       decoder_1_out2, decoder_1_out3, EN, EnR, ENRX, not_2_out, not_3_out, or_1_out, or_2_out, Run, STOP;
  wire [1:0] SELD, SELS;
  wire [2:0] OPCODE, R1_q_2, R2_q_2, R3_q_2, R4_q_2;
  wire [3:0] R1_q, R2_q, R3_q, R4_q;
  wire [6:0] adder_1_out, adder_2_out, multiplexer_1_out, multiplexer_2_out, not_1_out, Result,
       shifter_1_out, shifter_2_out;
  wire [7:0] multiplexer_4_out, PC_q, RX_q;
  wire [7:7] nor_1_out, xor_1_out;
  wire [14:0] rom_1_data;

  Decoder #(.select(2)) decoder_1 (
    .out0(decoder_1_out0), .out1(decoder_1_out1), .out2(decoder_1_out2), .out3(decoder_1_out3), .sel(SELD),
    .en(EnR));
  LED led_1 (.in(STOP));
  Register #(.width(7)) R1 (.D(Result), .en(decoder_1_out0), .clk(clock_1_out), .Q({R1_q_2, R1_q}), .clr(CLR));
  Register #(.width(7)) R2 (.D(Result), .en(decoder_1_out1), .clk(clock_1_out), .Q({R2_q_2, R2_q}), .clr(CLR));
  Register #(.width(7)) R3 (.D(Result), .en(decoder_1_out2), .clk(clock_1_out), .Q({R3_q_2, R3_q}), .clr(CLR));
  Register #(.width(7)) R4 (.D(Result), .en(decoder_1_out3), .clk(clock_1_out), .Q({R4_q_2, R4_q}), .clr(CLR));
  Clock clock_1 (.out(clock_1_out));
  or or_1 (or_1_out, Run, and_1_out);
  Button u_Run (.out(Run));
  and and_1 (and_1_out, clock_1_out, ~STOP);  // AND_Gate
  Hex_Digit_Display hex_digit_display_1 (.value({1'b0, R1_q_2}));  // open: dp
  Hex_Digit_Display hex_digit_display_2 (.value({1'b0, R3_q_2}));  // open: dp
  Counter PC (.load(Run), .clk(or_1_out), .D(in_1), .Q(PC_q));  // open: clr, up, count, carry
  Hex_Digit_Display hex_digit_display_3 (.value(R1_q));  // open: dp
  Hex_Digit_Display hex_digit_display_4 (.value({1'b0, R2_q_2}));  // open: dp
  Hex_Digit_Display hex_digit_display_5 (.value(R2_q));  // open: dp
  Hex_Digit_Display hex_digit_display_6 (.value(R3_q));  // open: dp
  Hex_Digit_Display hex_digit_display_7 (.value({1'b0, R4_q_2}));  // open: dp
  Hex_Digit_Display hex_digit_display_8 (.value(R4_q));  // open: dp
  Multiplexer #(.select(2), .width(7)) multiplexer_1 (
    .in0({R1_q_2, R1_q}), .in1({R2_q_2, R2_q}), .in2({R3_q_2, R3_q}), .in3({R4_q_2, R4_q}),
    .out(multiplexer_1_out), .sel(SELD));
  Multiplexer #(.select(2), .width(7)) multiplexer_2 (
    .in0({R1_q_2, R1_q}), .in1({R2_q_2, R2_q}), .in2({R3_q_2, R3_q}), .in3({R4_q_2, R4_q}),
    .out(multiplexer_2_out), .sel(SELS));
  assign not_1_out = ~multiplexer_2_out;  // NOT_Gate not_1, 7 bits wide
  ROM #(.dataWidth(16)) rom_1 (.addr(PC_q), .data({EN, rom_1_data[14], OPCODE, SELD, SELS, rom_1_data[6:0]}));
  Adder #(.width(7)) adder_1 (.a(multiplexer_1_out), .b(multiplexer_2_out), .out(adder_1_out));  // open: cin, cout
  Adder #(.width(7)) adder_2 (.a(multiplexer_1_out), .b(not_1_out), .out(adder_2_out), .cin(1'b1));  // open: cout
  Shifter #(.width(7)) shifter_1 (.in(multiplexer_1_out), .\dist (3'b001), .out(shifter_1_out));
  Shifter #(.shift("lr"), .width(7)) shifter_2 (.in(multiplexer_1_out), .\dist (3'b001), .out(shifter_2_out));
  nor nor_1 (nor_1_out[7], multiplexer_1_out[0], multiplexer_1_out[1], multiplexer_1_out[2], multiplexer_1_out[3], multiplexer_1_out[4], multiplexer_1_out[5], multiplexer_1_out[6]);
  ExactlyOne xor_1 (
    .out(xor_1_out[7]), .in0(multiplexer_1_out[0]), .in1(multiplexer_1_out[1]), .in2(multiplexer_1_out[2]),
    .in3(multiplexer_1_out[3]), .in4(multiplexer_1_out[4]), .in5(multiplexer_1_out[5]),
    .in6(multiplexer_1_out[6]));
  Multiplexer #(.select(3), .width(7)) multiplexer_3 (
    .in0(multiplexer_1_out), .in1(rom_1_data[6:0]), .in2(adder_1_out), .in3(adder_2_out),
    .in4(shifter_1_out), .in5(shifter_2_out), .in6({7{1'b0}}), .in7({7{1'b0}}), .out(Result), .sel(OPCODE));
  Multiplexer #(.width(8)) multiplexer_4 (
    .in0({nor_1_out[7], multiplexer_1_out}), .in1({xor_1_out[7], multiplexer_1_out}),
    .out(multiplexer_4_out), .sel(OPCODE[0]));
  Comparator #(.width(16)) comparator_1 (
    .a({EN, rom_1_data[14], OPCODE, SELD, SELS, rom_1_data[6:0]}), .b({16{1'b1}}), .eq(CLR));  // open: gt, lt
  Comparator #(.width(16)) comparator_2 (
    .a({EN, rom_1_data[14], OPCODE, SELD, SELS, rom_1_data[6:0]}), .b(16'hfffe), .eq(STOP));  // open: gt, lt
  Register RX (.D(multiplexer_4_out), .en(ENRX), .clk(clock_1_out), .Q(RX_q), .clr(CLR));
  Hex_Digit_Display hex_digit_display_9 (.value(RX_q[7:4]));  // open: dp
  Hex_Digit_Display hex_digit_display_10 (.value(RX_q[3:0]));  // open: dp
  Comparator #(.width(3)) comparator_3 (.a(OPCODE), .b(3'b110), .eq(comparator_3_eq));  // open: gt, lt
  Comparator #(.width(3)) comparator_4 (.a(OPCODE), .b(3'b111), .eq(comparator_4_eq));  // open: gt, lt
  not not_2 (not_2_out, STOP);
  and and_2 (EnR, EN, not_2_out);
  or or_2 (or_2_out, comparator_3_eq, comparator_4_eq);
  not not_3 (not_3_out, STOP);
  and and_3 (ENRX, or_2_out, not_3_out);

  // Other names for the same wires on the sheet: PCODE = OPCODE[0]

  // Notes on the sheet:
  //   regesters
  //   Rd
  //   Rs
  //   Control Unit
  //   contents of rom_1 (hex, n*v repeats v):
  //   ffff 8835 8a25 9080 fffe 0 ffff 8807 8a07 a000 a000 a000 9080 9080 fffe 0 0 0 ffff 8844 8a23 9880
  //   fffe 4*0 ffff 8878 a800 a800 fffe 4*0 ffff 8878 b000 fffe 8*0 ffff 8879 b800 fffe
  //   Rd+Rs
  //   Rd-Rs
  //   ROM
  //   ALU
  //   S1
  //   OPP CODE
  //   MOV-->000
  //   IMM-->001
  //   ADD-->010
  //   SUB-->011
  //   LSL-->100
  //   LSR-->100
  //   PODD-->110
  //   PEVEN-->111
  //   Enable circuits
endmodule
